// Logisim project S11219545_A3.circ as structural Verilog: 1 circuit, main circuit main
module main (
  input  A,
  input  B,
  input  C,
  output D
);

  wire nand_2_out, nand_3_out, nand_4_out, nand_5_out, nand_out;

  nand \nand  (nand_out, A, A);
  nand nand_2 (nand_2_out, B, B);
  nand nand_3 (nand_3_out, C, C);
  nand nand_4 (nand_4_out, A, nand_3_out);
  nand nand_5 (nand_5_out, nand_out, C);
  nand nand_6 (D, nand_5_out, nand_2_out, nand_4_out);

  // Notes on the sheet:
  //   Not A
  //   Not B
  //   Not C
endmodule
